# Fritzing sketch Termostato_stripboard (saved by Fritzing 0.9.2b)
stripboards: 1

parts:
  FTDI = female pin header, 6 pins [form="♀ (female)"]
  C1 = Ceramic Capacitor [capacitance=100nF package="100 mil [THT, multilayer]"]
  U1 = atmega328 [package=dip]
  R1 = Resistor [tolerance=±5% resistance=220 package=THT]
  C2 = Ceramic Capacitor [capacitance=100nF package="100 mil [THT, multilayer]"]
  C3 = Ceramic Capacitor [capacitance=100nF package="100 mil [THT, multilayer]"]
  LCD = female pin header, 8 pins [form="♀ (female)"]
  R2 = Temperature Sensor (Thermistor) [thermistor_type=NTC package=THT]
  R3 = Resistor [tolerance=±5% resistance=220 package=THT]
  NRF24_2 = female pin header, 4 pins [form="♀ (female)"]
  NRF24_1 = female pin header, 4 pins [form="♀ (female)"]
  C5 = Electrolytic Capacitor [capacitance=1µF package="100 mil [THT, electrolytic]"]  # not connected
  C6 = Electrolytic Capacitor [capacitance=1µF package="100 mil [THT, electrolytic]"]  # not connected
  R4 = Resistor [tolerance=±5% resistance=220 package=THT]
  R5 = Resistor [tolerance=±5% resistance=220 package=THT]
  SW1 = male pin header, 2 pins [form="♂ (male)"]
  SW2 = male pin header, 2 pins [form="♂ (male)"]
  DS3231 = male pin header, 5 pins [form="♂ (male)"]
  R7 = Trimmer Potentiometer [maximum_resistance=10kΩ package=THT]
  R8 = Resistor [tolerance=±5% resistance=100 package=THT]

nets:
  N1: FTDI.pin1, C1.0
  N2: FTDI.pin2, U1.D1_(TX)
  N3: FTDI.pin3, U1.D0_(RX)
  N4: FTDI.pin4, U1.VCC, U1.AVCC, R1.Pin_0, C2.1, C3.0, LCD.pin3, NRF24_2.pin1, SW1.pin1, SW2.pin1, DS3231.pin5
  N5: FTDI.pin6, U1.GND, C2.0, C3.1, LCD.pin1, R2.pin_0, R3.Pin_1, NRF24_1.pin1, R4.Pin_1, R5.Pin_1, DS3231.pin1
  N6: C1.1, U1.RESET, R1.Pin_1
  N7: U1.D2, R4.Pin_0, SW1.pin2
  N8: U1.D3_(PWM), R5.Pin_0, SW2.pin2
  N9: U1.D4, LCD.pin8
  N10: U1.D5_(PWM), LCD.pin4
  N11: U1.D6_(PWM), LCD.pin5
  N12: U1.D7, LCD.pin6
  N13: U1.D8, LCD.pin7
  N14: U1.D9_(PWM), NRF24_1.pin2
  N15: U1.D10_(PWM), NRF24_2.pin2
  N16: U1.D11_(PWM), NRF24_2.pin3
  N17: U1.D12, NRF24_1.pin4
  N18: U1.D13, NRF24_1.pin3
  N19: U1.A0, R2.pin_1
  N20: U1.A2, R3.Pin_0
  N21: U1.A3, R7.leg1, R7.leg2
  N22: U1.A4, DS3231.pin4
  N23: U1.A5, DS3231.pin3
  N24: LCD.pin2, R8.Pin_1
  N25: R7.wiper, R8.Pin_0
